# Fritzing sketch schema (saved by Fritzing 0.9.3b)
breadboards: 1

parts:
  Raspberry_Pi_1 = Raspberry Pi 3 [part_number=RPI-3-V1.2]
  LED1 = LED - 5mm [color="Red (633nm)" package="5 mm [THT]"]
  LED2 = LED - 5mm [color="Yellow (585nm)" package="5 mm [THT]"]
  LED3 = LED - 5mm [color="Green (555nm)" package="5 mm [THT]"]
  R1 = Resistor [tolerance=±5% resistance=220 package=THT]
  R2 = Resistor [tolerance=±5% resistance=220 package=THT]
  R3 = Resistor [tolerance=±5% resistance=220 package=THT]
  S1 = Pushbutton [package="[THT]"]
  R4 = Resistor [tolerance=±5% resistance=10k package=THT]
  R5 = Resistor [tolerance=±5% resistance=10k package=THT]
  LCD1 = LCD screen
  Componente1 = FTDI Basic Programmer
  LCM1602_IIC1 = LCM1602 IIC [part_number="LCM1602 IIC" chip_label="LCM1602 IIC" package="DIP (Dual Inline) [THT]"]
  Q2 = NPN-Transistor [package="TO92 [THT]"]
  buz1 = Piezo Buzzer
  R6 = Resistor [tolerance=±5% resistance=2k package=THT]

nets:
  3V3: Raspberry_Pi_1.3v3, Raspberry_Pi_1.3V3, R5.Pin_1, LCM1602_IIC1.VCC, buz1.pin_1
  N1: Raspberry_Pi_1.GPIO2, LCM1602_IIC1.SDA
  N2: Raspberry_Pi_1.GPIO3, LCM1602_IIC1.SCL
  GND: Raspberry_Pi_1.GND, LED1.cathode, LED2.cathode, LED3.cathode, S1.Pin_3, S1.Pin_4, Componente1.GND, LCM1602_IIC1.GND, Q2.E
  N3: Raspberry_Pi_1.GPIO17, R4.Pin_0
  N4: Raspberry_Pi_1.GPIO13, R6.Pin_1
  N5: Raspberry_Pi_1.GPIO19, R3.Pin_0
  N6: Raspberry_Pi_1.GPIO26, R2.Pin_0
  N7: Raspberry_Pi_1.GPIO21, R1.Pin_0
  N8: Raspberry_Pi_1.GPIO15, Componente1.TXO
  N9: Raspberry_Pi_1.GPIO14, Componente1.RXI
  N10: LED1.anode, R1.Pin_1
  N11: LED2.anode, R2.Pin_1
  N12: LED3.anode, R3.Pin_1
  N13: S1.Pin_1, S1.Pin_2, R4.Pin_1, R5.Pin_0
  VSS: LCD1.VSS, LCM1602_IIC1.VSS
  VDD: LCD1.VDD, LCM1602_IIC1.VDD
  N14: LCD1.V0, LCM1602_IIC1.V0
  N15: LCD1.RS, LCM1602_IIC1.RS
  N16: LCD1.R/W, LCM1602_IIC1.RW
  N17: LCD1.E, LCM1602_IIC1.E
  N18: LCD1.DB0, LCM1602_IIC1.D0
  N19: LCD1.DB1, LCM1602_IIC1.D1
  N20: LCD1.DB2, LCM1602_IIC1.D2
  N21: LCD1.DB3, LCM1602_IIC1.D3
  N22: LCD1.DB4, LCM1602_IIC1.D4
  N23: LCD1.DB5, LCM1602_IIC1.D5
  N24: LCD1.DB6, LCM1602_IIC1.D6
  N25: LCD1.DB7, LCM1602_IIC1.D7
  N26: LCD1.LED+, LCM1602_IIC1.A
  N27: LCD1.LED-, LCM1602_IIC1.K
  N28: Q2.B, R6.Pin_0
  N29: Q2.C, buz1.pin_2

custom parts:
  LCM1602 IIC: I2C-Module to use a 1602 or 2004 LCD on with the wire.h libory Serial LCD Modul
  Piezo Buzzer: Part from https://www.nutsvolts.com/magazine/article/november2012_SmileysWorkshop modified to be .3 in spacing to match the adafruit buzzer 5V breadboard friendly part.
